# Fritzing sketch Motor (saved by Fritzing 0.9.3b)
breadboards: 1

parts:
  Mod1 = Raspberry Pi 4B
  M2 = DC Motor
  JACK1 = 2.1mm Barrel Jack with Terminal Block
  M1 = DC Motor
  L298N1 = L298N DC motor driver
  R1 = Resistor [tolerance=±5% resistance=510 package=THT]
  LED1 = LED - 5mm [color="Red (633nm)" package="5 mm [THT]"]
  R2 = Resistor [tolerance=±5% resistance=510 package=THT]
  LED2 = LED - 5mm [color="Red (633nm)" package="5 mm [THT]"]

nets:
  GND: Mod1.GND, JACK1.NEG, L298N1.GND, LED1.cathode, LED2.cathode
  N1: Mod1.GPIO14, L298N1.IN1
  N2: Mod1.GPIO15, L298N1.IN2
  N3: Mod1.GPIO23, L298N1.IN3
  N4: Mod1.GPIO24, L298N1.IN4
  N5: Mod1.GPIO25, L298N1.ENA, R1.Pin_0
  N6: Mod1.GPIO7, L298N1.ENB, R2.Pin_0
  N7: M2.pin_1, L298N1.OUT4
  N8: M2.pin_2, L298N1.OUT3
  N9: JACK1.POS, L298N1.12V
  N10: M1.pin_1, L298N1.OUT2
  N11: M1.pin_2, L298N1.OUT1
  N12: R1.Pin_1, LED1.anode
  N13: R2.Pin_1, LED2.anode

custom parts:
  L298N DC motor driver: 2x DC motor driver with 78M05 positive voltage regulator (7..35 V) L298N: max 46 V, 2 A Set 5 V Enable jumper to enable 5 V regultor (needed for the L298N) and +5 V output at screw terminal or supply external +5 V at screw terminal Set ENA and/or ENB to +5 V to enable motor permanently or supply ENA and/or ENB with PWM signal IN1 and IN2 set rotation directory for motor A (OUT1/OUT2) IN2 and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
